# Fritzing sketch PCB (saved by Fritzing 0.9.3b)
perfboards: 1

parts:
  C7 = Ceramic Capacitor [capacitance=100nF package="100 mil [THT, multilayer]"]
  IC4 = MICROCONTROLLER [package=dil28-3-simon]
  C8 = Ceramic Capacitor [capacitance=100nF package="100 mil [THT, multilayer]"]
  XTAL4 = Crystal [frequency="16 Mhz" package=THT]
  J2 = male pin header, 7 pins [form="♂ (male)"]
  U2 = RELAY [package=relay-g5q]  # not connected
  C9 = Ceramic Capacitor [capacitance=0.1µF package="100 mil [THT, multilayer]"]

nets:
  N1: C7.0, IC4.PB6(XTAL1_TOSC1), XTAL4.pin_1
  N2: C7.1, IC4.GND, IC4.AGND, C8.0, J2.pin1, J2.pin6, C9.0
  N3: IC4.PD3(INT1), J2.pin3
  N4: IC4.PD4(XCK_T0), J2.pin2
  N5: IC4.VCC, IC4.AVCC, J2.pin4, C9.1
  N6: IC4.PB7(XTAL2_TOSC2), C8.1, XTAL4.pin_0
  N7: IC4.PC2(ADC2), J2.pin7
